# Fritzing sketch V2 Sketch (saved by Fritzing 0.9.10b)
breadboards: 2

parts:
  부품1 = Arduino Mega 2560 (Rev3)
  M1 = RioRand LM2596
  M2 = RioRand LM2596
  J1 = Camdenboss CTB0158-2 [part_number=CTB0158-2 package=THT]
  VCC1 = Battery
  J2 = Camdenboss CTB0158-4 [part_number=CTB0158-4 package=THT]
  J3 = Camdenboss CTB0158-4 [part_number=CTB0158-4 package=THT]
  M3 = RioRand LM2596
  J4 = Camdenboss CTB0158-2 [part_number=CTB0158-2 package=THT]
  M4 = DC Motor [voltage_(max)=6V voltage_(min)=3V]
  S1 = H-Bridge with L298N
  S2 = H-Bridge with L298N
  M5 = DC Motor [voltage_(max)=6V voltage_(min)=3V]
  S3 = H-Bridge with L298N
  S4 = H-Bridge with L298N
  M6 = DC Motor [voltage_(max)=6V voltage_(min)=3V]
  M7 = DC Motor [voltage_(max)=6V voltage_(min)=3V]
  Mod1 = Raspberry Pi Pico
  BT1 = Bluetooth HC-06u [package=THT]
  VCC2 = Battery

nets:
  N1: 부품1.D17_PWM/RX2, Mod1.pin_6
  N2: 부품1.D16_PWM/TX2, Mod1.pin_7
  GND: 부품1.GND, J4.pin1, Mod1.pin_3, Mod1.pin_8, Mod1.pin_13, Mod1.pin_18, Mod1.pin_23, Mod1.pin_28, Mod1.pin_33, Mod1.pin_38, BT1.GND
  5V: 부품1.VIN, J4.pin2, S1.5V, S2.5V, S3.5V, S4.5V, Mod1.pin_39, BT1.VCC
  N3: M1.Pin_1, M2.Pin_1, J1.pin2, M3.Pin_1
  N4: M1.Pin_2, M2.Pin_2, J1.pin1, M3.Pin_2
  N5: M1.Pin_3, J2.terminal_3, J2.terminal_4
  N6: M1.Pin_4, J2.terminal_1, J2.terminal_2
  N7: M2.Pin_3, J3.terminal_3, J3.terminal_4
  N8: M2.Pin_4, J3.terminal_1, J3.terminal_2
  N9: J1.terminal_1, VCC1.-, VCC2.-
  N10: J1.terminal_2, VCC1.+, VCC2.+
  N11: J2.pin1, S3.GND
  N12: J2.pin2, S1.GND
  N13: J2.pin3, S3.12V
  N14: J2.pin4, S1.12V
  N15: J3.pin1, S2.GND
  N16: J3.pin2, S4.GND
  N17: J3.pin3, S2.12V
  N18: J3.pin4, S4.12V
  N19: M3.Pin_3, J4.terminal_2
  N20: M3.Pin_4, J4.terminal_1
  N21: M4.pin_1, S1.M2-02
  N22: M4.pin_2, S1.M2-01
  N23: S1.IN3, Mod1.pin_15
  N24: S1.IN4, Mod1.pin_14
  N25: S1.ENB, Mod1.pin_21
  N26: S2.ENA, Mod1.pin_22
  N27: S2.IN1, Mod1.pin_17
  N28: S2.IN2, Mod1.pin_16
  N29: S2.M1-01, M5.pin_2
  N30: S2.M1-02, M5.pin_1
  N31: S3.ENA, Mod1.pin_19
  N32: S3.IN1, Mod1.pin_10
  N33: S3.IN2, Mod1.pin_9
  N34: S3.M1-01, M7.pin_2
  N35: S3.M1-02, M7.pin_1
  N36: S4.IN3, Mod1.pin_12
  N37: S4.IN4, Mod1.pin_11
  N38: S4.ENB, Mod1.pin_20
  N39: S4.M2-01, M6.pin_2
  N40: S4.M2-02, M6.pin_1
  N41: Mod1.pin_1, BT1.RXD
  N42: Mod1.pin_2, BT1.TXD

custom parts:
  Battery: Your standard 2x 18650 battery pack (14.7 Volts)
  H-Bridge with L298N: h-bridge
  Raspberry Pi Pico: Raspberry Pi Pico. Based around the RP2040 microcontroller the Pico is a low cost microcontroller device bringing Raspberry Pi quality, cost, and easy of use to the microcontroller space. Jan 2021, Split part in to two versions: tht (this one) and SMD. This one will drill holes for a .1 in header in pcb to allow plugging in the module as well as providing pads to solder the module to the top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
  Bluetooth HC-06u: Bluetooth HC-06 - face up, pins down 16.5mm x 37.5mm PCB
